// Logisim project s-mips.circ as structural Verilog
module S_MIPS_Board (
  input  DESHABILITAR_DISPATCHER,
  output halt
);

  wire button_1_out, CLK, CS, d_ff_1_q, LCLR, LoadRAM, LoadRAMOn, LW, R_R_W, R_W, ram_dispatcher_1_finished,
       RCS, Reset_out, RST, TTY_EN;
  wire [2:0] KDB;
  wire [3:0] LMask, Mask, ram_1_read_time, ram_1_write_time, RMask;
  wire [6:0] KDB_DATA, TTY_DATA;
  wire [15:0] Addr, LAddr, RAddr;
  wire [31:0] I0, I1, I2, I3, LData, ram_1_data_out_0, ram_1_data_out_1, ram_1_data_out_2, ram_1_data_out_3,
       RI0, RI1, RI2, RI3;

  TTY #(.rows(25), .cols(80)) tty_1 (.data(TTY_DATA), .clk(CLK), .we(TTY_EN), .clr(RST));
  not not_1 (LoadRAMOn, ram_dispatcher_1_finished);
  RAM_Dispatcher ram_dispatcher_1 (
    .WriteTime(ram_1_write_time), .Clock(CLK), .Data(LData), .Address(LAddr), .Mask(LMask),
    .Finished(ram_dispatcher_1_finished), .Write(LW), .CLR(LCLR));
  Keyboard #(.buflen(64)) keyboard_1 (.clk(CLK), .re(KDB[0]), .avail(KDB[2]), .data(KDB_DATA));  // open: clr
  RAM ram_1 (
    .Address(RAddr), .Data_Out_0(ram_1_data_out_0), .Data_Out_1(ram_1_data_out_1),
    .Data_Out_2(ram_1_data_out_2), .Data_Out_3(ram_1_data_out_3), .Data_In_0(RI0), .Data_In_1(RI1),
    .Data_In_2(RI2), .Data_In_3(RI3), .Mask(RMask), .nRead_Write(R_R_W), .Chip_Select(RCS),
    .Read_Time(ram_1_read_time), .Reset(button_1_out), .Write_Time(ram_1_write_time));
  Button button_1 (.out(button_1_out));
  D_Flip_Flop d_ff_1 (.clk(CLK), .D(1'b1), .Q(d_ff_1_q), .reset(Reset_out));  // open: Qn, preset, en
  Button Reset (.out(Reset_out));
  S_MIPS s_mips_1 (
    .Kbd_Enable(KDB[0]), .Address(Addr), .Kbd_Clear(KDB[1]), .Kbd_Available(KDB[2]), .RAM_In_0(I0),
    .Kbd_ASCII_Data(KDB_DATA), .RAM_In_1(I1), .TTY_Enable(TTY_EN), .RAM_In_2(I2), .RAM_In_3(I3),
    .TTY_ASCII_Data(TTY_DATA), .Reset(RST), .RAM_Out_0(ram_1_data_out_0), .Clock(CLK),
    .RAM_Out_1(ram_1_data_out_1), .Stop(halt), .RAM_Out_2(ram_1_data_out_2), .RAM_Out_3(ram_1_data_out_3),
    .Mask(Mask), .Read_Time(ram_1_read_time), .Write_Time(ram_1_write_time), .nRead_Write(R_W),
    .Chip_Select(CS));
  D_Flip_Flop d_ff_2 (.clk(CLK), .D(d_ff_1_q), .Qn(LCLR), .reset(Reset_out));  // open: Q, preset, en
  or or_1 (RST, LCLR, LoadRAM);
  Clock clock_1 (.out(CLK));
  Multiplexer #(.width(32), .enable("false")) multiplexer_1 (.in0(I0), .in1(LData), .out(RI0), .sel(LoadRAM));
  Multiplexer #(.width(32), .enable("false")) multiplexer_2 (.in0(I1), .in1(LData), .out(RI1), .sel(LoadRAM));
  Multiplexer #(.width(32), .enable("false")) multiplexer_3 (.in0(I2), .in1(LData), .out(RI2), .sel(LoadRAM));
  Multiplexer #(.width(32), .enable("false")) multiplexer_4 (.in0(I3), .in1(LData), .out(RI3), .sel(LoadRAM));
  and and_1 (LoadRAM, ~DESHABILITAR_DISPATCHER, LoadRAMOn);  // AND_Gate
  Multiplexer #(.width(16), .enable("false")) multiplexer_5 (.in0(Addr), .in1(LAddr), .out(RAddr), .sel(LoadRAM));
  Multiplexer #(.width(4), .enable("false")) multiplexer_6 (.in0(Mask), .in1(LMask), .out(RMask), .sel(LoadRAM));
  Multiplexer #(.enable("false")) multiplexer_7 (.in0(CS), .in1(LW), .out(RCS), .sel(LoadRAM));
  Multiplexer #(.enable("false")) multiplexer_8 (.in0(R_W), .in1(LW), .out(R_R_W), .sel(LoadRAM));

  // Notes on the sheet:
  //   NO MODIFICAR
  //   Keyboard
endmodule

module RAM (
  input  [15:0] Address,
  input  [31:0] Data_In_0,
  input  [31:0] Data_In_1,
  input  [31:0] Data_In_2,
  input  [31:0] Data_In_3,
  input  [3:0] Mask,
  input  nRead_Write,
  input  Chip_Select,
  input  Reset,
  output [31:0] Data_Out_0,
  output [31:0] Data_Out_1,
  output [31:0] Data_Out_2,
  output [31:0] Data_Out_3,
  output [3:0] Read_Time,
  output [3:0] Write_Time
);

  wire and_2_out, and_3_out, and_4_out, and_5_out, and_6_out, and_7_out, and_8_out, and_9_out, Changed, CLK,
       comparator_2_eq, comparator_3_eq, comparator_4_eq, comparator_5_eq, comparator_6_eq, Count,
       demultiplexer_3_out0, Idle, Idle_q, Load, Load0, Load1, nand_1_out, or_1_out, or_2_out, or_3_out,
       or_4_out, or_5_out, or_6_out, or_7_out, or_8_out, or_9_out, or_10_out, Proc_q, Update_Mem, Zero_Time;
  wire [3:0] counter_1_q, multiplexer_1_out, subtractor_1_out;
  wire [31:0] register_1_q, register_2_q, register_3_q, register_4_q, register_5_q;

  // Probe on 4'b0011
  // Probe on 4'b0010
  Multiplexer #(.width(4), .enable("false")) multiplexer_1 (
    .in0(4'b0011), .in1(4'b0010), .out(multiplexer_1_out), .sel(nRead_Write));
  or or_1 (or_1_out, Idle, Update_Mem);
  or or_2 (or_2_out, ~Chip_Select, Reset);  // OR_Gate
  Subtractor #(.width(4)) subtractor_1 (.a(multiplexer_1_out), .b(4'b0010), .out(subtractor_1_out));  // open: bin, bout
  D_Flip_Flop u_Idle (.clk(CLK), .D(or_1_out), .Q(Idle_q), .preset(or_2_out));  // open: Qn, en, reset
  Demultiplexer #(.enable("false")) demultiplexer_1 (.out0(Idle), .out1(Load0), .in(Idle_q), .sel(Changed));
  // Probe on counter_1_q
  Counter #(.width(4), .max('hf)) counter_1 (
    .load(Load), .D(subtractor_1_out), .count(Count), .Q(counter_1_q), .clk(CLK), .clr(or_3_out));  // open: carry
  or or_3 (or_3_out, ~Chip_Select, Reset);  // OR_Gate
  Comparator #(.width(4), .mode("unsigned")) comparator_1 (
    .a(4'b0000), .b(counter_1_q), .eq(Zero_Time));  // open: gt, lt
  or or_4 (or_4_out, Count, Load0, Load1);
  Register #(.width(32)) register_1 (.D(Data_In_0), .en(Chip_Select), .Q(register_1_q), .clk(CLK), .clr(or_5_out));
  or or_5 (or_5_out, ~Chip_Select, Reset);  // OR_Gate
  Register #(.width(32)) register_2 (.D(Data_In_1), .en(Chip_Select), .Q(register_2_q), .clk(CLK), .clr(or_6_out));
  or or_6 (or_6_out, ~Chip_Select, Reset);  // OR_Gate
  Register #(.width(32)) register_3 (.D(Data_In_2), .en(Chip_Select), .Q(register_3_q), .clk(CLK), .clr(or_7_out));
  or or_7 (or_7_out, ~Chip_Select, Reset);  // OR_Gate
  Register #(.width(32)) register_4 (.D(Data_In_3), .en(Chip_Select), .Q(register_4_q), .clk(CLK), .clr(or_8_out));
  or or_8 (or_8_out, ~Chip_Select, Reset);  // OR_Gate
  Register #(.width(32)) register_5 (
    .D({{11{1'b1}}, nRead_Write, Mask, Address}), .en(Chip_Select), .Q(register_5_q), .clk(CLK),
    .clr(or_9_out));
  or or_9 (or_9_out, ~Chip_Select, Reset);  // OR_Gate
  D_Flip_Flop Proc (.clk(CLK), .D(or_4_out), .Q(Proc_q), .reset(or_10_out));  // open: Qn, preset, en
  or or_10 (or_10_out, ~Chip_Select, Reset);  // OR_Gate
  Demultiplexer #(.enable("false")) demultiplexer_2 (
    .out0(Count), .out1(Update_Mem), .in(demultiplexer_3_out0), .sel(Zero_Time));
  Demultiplexer #(.enable("false")) demultiplexer_3 (
    .out0(demultiplexer_3_out0), .out1(Load1), .in(Proc_q), .sel(Changed));
  Clock clock_1 (.out(CLK));
  Comparator #(.width(32)) comparator_2 (.a(register_1_q), .b(Data_In_0), .eq(comparator_2_eq));  // open: gt, lt
  Comparator #(.width(32)) comparator_3 (.a(register_2_q), .b(Data_In_1), .eq(comparator_3_eq));  // open: gt, lt
  Comparator #(.width(32)) comparator_4 (.a(register_3_q), .b(Data_In_2), .eq(comparator_4_eq));  // open: gt, lt
  Comparator #(.width(32)) comparator_5 (.a(register_4_q), .b(Data_In_3), .eq(comparator_5_eq));  // open: gt, lt
  Comparator #(.width(32)) comparator_6 (
    .a(register_5_q), .b({{11{1'b1}}, nRead_Write, Mask, Address}), .eq(comparator_6_eq));  // open: gt, lt
  nand nand_1 (nand_1_out, comparator_6_eq, comparator_2_eq, comparator_3_eq, comparator_4_eq, comparator_5_eq);
  and and_1 (Changed, nand_1_out, Chip_Select);
  or or_11 (Load, Count, Load1, Load0);
  and and_2 (and_2_out, Mask[0], Update_Mem, nRead_Write);
  and and_3 (and_3_out, Mask[1], Update_Mem, nRead_Write);
  and and_4 (and_4_out, Mask[2], Update_Mem, nRead_Write);
  and and_5 (and_5_out, Mask[3], Update_Mem, nRead_Write);
  RAM_part #(.addrWidth(16), .dataWidth(32), .bus("separate")) ram_1 (
    .addr(Address), .din(Data_In_0), .data(Data_Out_0), .str(and_2_out), .sel(Chip_Select), .clk(CLK),
    .ld(and_6_out), .clr(Reset));
  and and_6 (and_6_out, ~nRead_Write, Idle);  // AND_Gate
  RAM_part #(.addrWidth(16), .dataWidth(32), .bus("separate")) ram_2 (
    .addr(Address), .din(Data_In_1), .data(Data_Out_1), .str(and_3_out), .sel(Chip_Select), .clk(CLK),
    .ld(and_7_out), .clr(Reset));
  and and_7 (and_7_out, ~nRead_Write, Idle);  // AND_Gate
  RAM_part #(.addrWidth(16), .dataWidth(32), .bus("separate")) ram_3 (
    .addr(Address), .din(Data_In_2), .data(Data_Out_2), .str(and_4_out), .sel(Chip_Select), .clk(CLK),
    .ld(and_8_out), .clr(Reset));
  and and_8 (and_8_out, ~nRead_Write, Idle);  // AND_Gate
  RAM_part #(.addrWidth(16), .dataWidth(32), .bus("separate")) ram_4 (
    .addr(Address), .din(Data_In_3), .data(Data_Out_3), .str(and_5_out), .sel(Chip_Select), .clk(CLK),
    .ld(and_9_out), .clr(Reset));
  and and_9 (and_9_out, ~nRead_Write, Idle);  // AND_Gate

  assign Read_Time = 4'b0011;
  assign Write_Time = 4'b0010;

  // Other names for the same wires on the sheet: M0 = Mask[0]; M1 = Mask[1]; M2 = Mask[2]; M3 = Mask[3];
  //   RW = nRead_Write; CLR = Reset; CS = Chip_Select; Load2 = Count

  // Notes on the sheet:
  //   NO MODIFICAR
  //   excepto quizás los valores RT y WT
  //   BANK0
  //   BANK1
  //   BANK2
  //   BANK3
endmodule

module S_MIPS (
  input  Kbd_Available,
  input  [6:0] Kbd_ASCII_Data,
  input  [31:0] RAM_Out_0,
  input  [31:0] RAM_Out_1,
  input  Reset,
  input  [31:0] RAM_Out_2,
  input  Clock,
  input  [31:0] RAM_Out_3,
  input  [3:0] Read_Time,
  input  [3:0] Write_Time,
  output Kbd_Enable,
  output [15:0] Address,
  output Kbd_Clear,
  output TTY_Enable,
  output [6:0] TTY_ASCII_Data,
  output Stop,
  output [31:0] RAM_In_0,
  output [31:0] RAM_In_1,
  output [31:0] RAM_In_2,
  output [31:0] RAM_In_3,
  output [3:0] Mask,
  output nRead_Write,
  output Chip_Select
);

  Branch_Control branch_control_1 ();  // open: bne, blez, bgtz, bltz, ZF, NF, j, jr, beq, rs, pc_in, offset, target, pc_out
  Data_Path data_path_1 ();  // open: func_code, op_code, offset, kbd, rst, clk, in_7, in_9, kbd_avail, RW, nop, pop, andi, add, slt, ori, sub, sltu, xori, mult, jr, slti, mulu, mfhi, sltiu, div, mflo, lw, divu, halt, sw, and, kbd_2, beq, or, rnd, bne, nor, tty, blez, xor, j, bgtz, push, addi, bltz, enable_md, Instruction
  ID id_1 ();  // open: in_1, is_nop, is_add, is_sub, is_mul, is_mulu, is_div, is_divu, is_slt, is_sltu, is_and, is_or, is_nor, is_xor, is_andi, is_mfhi, is_ori, is_xori, is_addi, is_beq, is_slti, is_bne, is_blez, is_mflo, is_sltiu, is_bgtz, is_bltz, is_lw, is_sw, is_j, is_jr, is_push, is_pop, is_kbd, is_rnd, is_tty, is_halt, rd, rt, rs, target, offset, R1, R3, R2, inm

  // Other names for the same wires on the sheet: CLK = Clock; CLR = Reset; CS = Chip_Select;
  //   KBD_AVAIL = Kbd_Available; KBD_CLR = Kbd_Clear; KBD_DATA[6:0] = Kbd_ASCII_Data; RAM_A[15:0] = Address;
  //   RAM_INPUT_0[31:0] = RAM_In_0; RAM_INPUT_1[31:0] = RAM_In_1; RAM_INPUT_2[31:0] = RAM_In_2;
  //   RAM_INPUT_3[31:0] = RAM_In_3; RAM_MASK[3:0] = Mask; RAM_OUTPUT_0[31:0] = RAM_Out_0;
  //   RAM_OUTPUT_1[31:0] = RAM_Out_1; RAM_OUTPUT_2[31:0] = RAM_Out_2; RAM_OUTPUT_3[31:0] = RAM_Out_3;
  //   RW = nRead_Write; TTY_DATA[6:0] = TTY_ASCII_Data

  // Notes on the sheet:
  //   RAM ADDRESS
  //   DATA FROM RAM
  //   DATA TO RAM
  //   DATA WRITE MASK
  //   RAM TIMING
  //   RAM CONTROL
  //   KEYBOARD
  //   TTY
  //   SEQUENCING
endmodule

module RAM_Dispatcher (
  input  [3:0] WriteTime,
  input  Clock,
  input  CLR,
  output [31:0] Data,
  output [15:0] Address,
  output [3:0] Mask,
  output Finished,
  output Write
);

  wire demultiplexer_2_out1, demultiplexer_3_out1, End, IDLE_q, IncAddr, Load, or_1_out, or_2_out, While_q,
       WriteEnd;
  wire [3:0] counter_1_q;
  wire [31:0] CurrentAddress_q;

  Counter #(.width(32), .max('hffffffff)) CurrentAddress (
    .count(IncAddr), .Q({CurrentAddress_q[31:18], Address, CurrentAddress_q[1:0]}), .clk(Clock), .clr(CLR));  // open: load, D, carry
  or or_1 (or_1_out, IncAddr, demultiplexer_3_out1, Finished);
  D_Flip_Flop IDLE (.clk(Clock), .D(or_1_out), .Q(IDLE_q), .preset(CLR));  // open: Qn, en, reset
  Demultiplexer #(.enable("false")) demultiplexer_1 (.out0(Load), .out1(Finished), .in(IDLE_q), .sel(End));
  D_Flip_Flop While (.clk(Clock), .D(or_2_out), .Q(While_q), .reset(CLR));  // open: Qn, preset, en
  or or_2 (or_2_out, Write, Load);
  RAM_part #(.addrWidth(18), .dataWidth(32)) ram_1 (
    .addr({Address, CurrentAddress_q[1:0]}), .data(Data), .clk(Clock));  // open: sel, ld, clr
  Demultiplexer #(.enable("false")) demultiplexer_2 (
    .out0(Write), .out1(demultiplexer_2_out1), .in(While_q), .sel(WriteEnd));
  Decoder #(.select(2)) decoder_1 (
    .out0(Mask[0]), .out1(Mask[1]), .out2(Mask[2]), .out3(Mask[3]), .sel(CurrentAddress_q[1:0]));  // open: en
  Demultiplexer #(.enable("false")) demultiplexer_3 (
    .out0(IncAddr), .out1(demultiplexer_3_out1), .in(demultiplexer_2_out1), .sel(End));
  Counter #(.width(4), .max('hf)) counter_1 (
    .load(Load), .D(WriteTime), .count(Write), .Q(counter_1_q), .clk(Clock));  // open: carry, clr
  Comparator #(.width(32)) comparator_1 (.a(Data), .b({32{1'b1}}), .eq(End));  // open: gt, lt
  Comparator #(.width(4)) comparator_2 (.a(4'b0000), .b(counter_1_q), .eq(WriteEnd));  // open: gt, lt

  // Other names for the same wires on the sheet: CLK = Clock; Count = Write; WT[3:0] = WriteTime
endmodule

module Register_File (
  input  MD,
  input  Reset,
  input  [31:0] DI,
  input  Clk,
  input  [4:0] A,
  input  [4:0] B,
  input  RW,
  input  [4:0] DA,
  input  [31:0] HI_value,
  input  [31:0] LO_value,
  output [31:0] HI_value_2,
  output [31:0] LO_value_2,
  output [31:0] RA,
  output [31:0] RB,
  output [31:0] Stack_Pointer
);

  wire R1, R2, R3, R4, R5, R6, R7, R8, R9, R10, R11, R12, R13, R14, R15, R16, R17, R18, R19, R20, R21, R22,
       R23, R24, R25, R26, R27, R28, R29, R30, R31;
  wire [31:0] O19, OR0, OR1, OR2, OR3, OR4, OR5, OR6, OR7, OR8, OR9, OR10, OR11, OR12, OR13, OR14, OR15,
       OR16, OR17, OR18, OR19, OR20, OR21, OR22, OR23, OR24, OR25, OR26, OR27, OR28, OR29, OR30;

  Register #(.width(32)) register_1 (.D({32{1'b0}}), .Q(OR0), .clk(Clk), .clr(Reset));  // open: en
  Register #(.width(32)) register_2 (.D(DI), .en(R8), .Q(OR8), .clk(Clk), .clr(Reset));
  Register #(.width(32)) register_3 (.D(DI), .en(R16), .Q(OR16), .clk(Clk), .clr(Reset));
  Register #(.width(32)) register_4 (.D(DI), .en(R24), .Q(OR24), .clk(Clk), .clr(Reset));
  Register #(.width(32)) register_5 (.D(DI), .en(R1), .Q(OR1), .clk(Clk), .clr(Reset));
  Register #(.width(32)) register_6 (.D(DI), .en(R9), .Q(OR9), .clk(Clk), .clr(Reset));
  Register #(.width(32)) register_7 (.D(DI), .en(R17), .Q(OR17), .clk(Clk), .clr(Reset));
  Register #(.width(32)) register_8 (.D(DI), .en(R25), .Q(OR25), .clk(Clk), .clr(Reset));
  Register #(.width(32)) register_9 (.D(DI), .en(R2), .Q(OR2), .clk(Clk), .clr(Reset));
  Register #(.width(32)) register_10 (.D(DI), .en(R10), .Q(OR10), .clk(Clk), .clr(Reset));
  Register #(.width(32)) register_11 (.D(DI), .en(R18), .Q(OR18), .clk(Clk), .clr(Reset));
  Register #(.width(32)) register_12 (.D(DI), .en(R26), .Q(OR26), .clk(Clk), .clr(Reset));
  Register #(.width(32)) register_13 (.D(DI), .en(R3), .Q(OR3), .clk(Clk), .clr(Reset));
  Register #(.width(32)) register_14 (.D(DI), .en(R11), .Q(OR11), .clk(Clk), .clr(Reset));
  Register #(.width(32)) register_15 (.D(DI), .en(R19), .Q(OR19), .clk(Clk), .clr(Reset));
  Register #(.width(32)) HI (.D(HI_value), .en(MD), .Q(HI_value_2), .clk(Clk), .clr(Reset));
  Register #(.width(32)) register_16 (.D(DI), .en(R27), .Q(OR27), .clk(Clk), .clr(Reset));
  Register #(.width(32)) register_17 (.D(DI), .en(R4), .Q(OR4), .clk(Clk), .clr(Reset));
  Register #(.width(32)) register_18 (.D(DI), .en(R12), .Q(OR12), .clk(Clk), .clr(Reset));
  Register #(.width(32)) register_19 (.D(DI), .en(R20), .Q(OR20), .clk(Clk), .clr(Reset));
  Register #(.width(32)) register_20 (.D(DI), .en(R28), .Q(OR28), .clk(Clk), .clr(Reset));
  Register #(.width(32)) register_21 (.D(DI), .en(R5), .Q(OR5), .clk(Clk), .clr(Reset));
  Register #(.width(32)) register_22 (.D(DI), .en(R13), .Q(OR13), .clk(Clk), .clr(Reset));
  Register #(.width(32)) register_23 (.D(DI), .en(R21), .Q(OR21), .clk(Clk), .clr(Reset));
  Register #(.width(32)) register_24 (.D(DI), .en(R29), .Q(OR29), .clk(Clk), .clr(Reset));
  Register #(.width(32)) LO (.D(LO_value), .en(MD), .Q(LO_value_2), .clk(Clk), .clr(Reset));
  Register #(.width(32)) register_25 (.D(DI), .en(R6), .Q(OR6), .clk(Clk), .clr(Reset));
  Register #(.width(32)) register_26 (.D(DI), .en(R14), .Q(OR14), .clk(Clk), .clr(Reset));
  Register #(.width(32)) register_27 (.D(DI), .en(R22), .Q(OR22), .clk(Clk), .clr(Reset));
  Register #(.width(32)) register_28 (.D(DI), .en(R30), .Q(OR30), .clk(Clk), .clr(Reset));
  Register #(.width(32)) register_29 (.D(DI), .en(R7), .Q(OR7), .clk(Clk), .clr(Reset));
  Register #(.width(32)) register_30 (.D(DI), .en(R15), .Q(OR15), .clk(Clk), .clr(Reset));
  Register #(.width(32)) register_31 (.D(DI), .en(R23), .Q(OR23), .clk(Clk), .clr(Reset));
  Register #(.width(32)) register_32 (.D(DI), .en(R31), .Q(Stack_Pointer), .clk(Clk), .clr(Reset));
  Decoder #(.select(5), .disabled(0)) decoder_1 (
    .out1(R1), .out2(R2), .out3(R3), .out4(R4), .out5(R5), .out6(R6), .out7(R7), .out8(R8), .out9(R9),
    .out10(R10), .out11(R11), .out12(R12), .out13(R13), .out14(R14), .out15(R15), .out16(R16), .out17(R17),
    .out18(R18), .out19(R19), .out20(R20), .out21(R21), .out22(R22), .out23(R23), .out24(R24), .out25(R25),
    .out26(R26), .out27(R27), .out28(R28), .out29(R29), .out30(R30), .out31(R31), .sel(DA), .en(RW));  // open: out0
  Multiplexer #(.select(5), .width(32), .disabled(0), .enable("false")) multiplexer_1 (
    .in1(OR1), .in2(OR2), .in3(OR3), .in4(OR4), .in5(OR5), .in6(OR6), .in7(OR7), .in8(OR8), .in9(OR9),
    .in10(OR10), .in11(OR11), .in12(OR12), .in13(OR13), .in14(OR14), .in15(OR15), .in16(OR16), .in17(OR17),
    .in18(OR18), .in19(O19), .in20(OR20), .in21(OR21), .in22(OR22), .in23(OR23), .in24(OR24), .in25(OR25),
    .in26(OR26), .in27(OR27), .in28(OR28), .in29(OR29), .in30(OR30), .in31(Stack_Pointer), .out(RA), .sel(A));  // open: in0
  Multiplexer #(.select(5), .width(32), .disabled(0), .enable("false")) multiplexer_2 (
    .in1(OR1), .in2(OR2), .in3(OR3), .in4(OR4), .in5(OR5), .in6(OR6), .in7(OR7), .in8(OR8), .in9(OR9),
    .in10(OR10), .in11(OR11), .in12(OR12), .in13(OR13), .in14(OR14), .in15(OR15), .in16(OR16), .in17(OR17),
    .in18(OR18), .in19(O19), .in20(OR20), .in21(OR21), .in22(OR22), .in23(OR23), .in24(OR24), .in25(OR25),
    .in26(OR26), .in27(OR27), .in28(OR28), .in29(OR29), .in30(OR30), .in31(Stack_Pointer), .out(RB), .sel(B));  // open: in0

  // Other names for the same wires on the sheet: HI_VALUE_t[31:0] = HI_value_2; LO_VALUE_t[31:0] = LO_value_2;
  //   OR31[31:0] = Stack_Pointer

  // Notes on the sheet:
  //   INPUT
  //   OUPUT
endmodule

module ABS (
  input  [31:0] A,
  output [31:0] A_2
);

  wire [31:0] and_1_out, and_2_out, EXT_Sign_A, negator_1_out, not_1_out;

  assign EXT_Sign_A = {{31{A[31]}}, A[31]};  // Bit_Extender bit_extender_1
  // Probe on A
  Negator #(.width(32)) negator_1 (.in(A), .out(negator_1_out));
  // Probe on A_2
  assign and_1_out = EXT_Sign_A & negator_1_out;  // AND_Gate and_1, 32 bits wide
  assign not_1_out = ~EXT_Sign_A;  // NOT_Gate not_1, 32 bits wide
  assign and_2_out = not_1_out & A;  // AND_Gate and_2, 32 bits wide
  assign A_2 = and_1_out | and_2_out;  // OR_Gate or_1, 32 bits wide

  // Other names for the same wires on the sheet: Sign_A = A[31]; A_t[31:0] = A_2

  // Notes on the sheet:
  //   INPUT
  //   OUTPUT
endmodule

module Branch_Control (
  input  beq,
  input  ZF,
  input  j,
  input  [31:0] rs,
  input  bne,
  input  NF,
  input  jr,
  input  blez,
  input  [15:0] offset,
  input  bgtz,
  input  [31:0] pc_in,
  input  bltz,
  input  [25:0] target,
  output [31:0] pc_out
);

  wire and_1_out, and_2_out, and_3_out, and_4_out, and_5_out, branch, gtz, lez, neq;
  wire [1:0] pc_selector;
  wire [31:0] bit_extender_1_out, branch_adress, pc_4, shifter_1_out;
  wire [31:28] j_adress;

  and and_1 (and_1_out, beq, ZF);
  and and_2 (and_2_out, bne, neq);
  and and_3 (and_3_out, blez, lez);
  and and_4 (and_4_out, bgtz, gtz);
  and and_5 (and_5_out, bltz, NF);
  not not_1 (neq, ZF);
  or or_1 (lez, ZF, NF);
  and and_6 (gtz, ~ZF, ~NF);  // AND_Gate
  or or_2 (branch, and_1_out, and_2_out, and_3_out, and_4_out, and_5_out);
  Bit_Extender #(.in_width(16), .out_width(32), .\type ("sign")) bit_extender_1 (.out(bit_extender_1_out));  // open: in
  Adder #(.width(32)) adder_1 (.a(32'h4), .b(pc_in), .out(pc_4));  // open: cin, cout
  Shifter #(.width(32)) shifter_1 (.in(bit_extender_1_out), .\dist (5'b00010), .out(shifter_1_out));
  Adder #(.width(32)) adder_2 (.a(pc_4), .b(shifter_1_out), .out(branch_adress));  // open: cin, cout
  Multiplexer #(.select(2), .width(32), .enable("false")) multiplexer_1 (
    .in0(pc_4), .in1({j_adress, target, 2'b00}), .in2(rs), .in3(branch_adress), .out(pc_out),
    .sel(pc_selector));
  or or_3 (pc_selector[0], j, branch);
  or or_4 (pc_selector[1], branch, jr);

  // Other names for the same wires on the sheet: eq = ZF; j_adress[27:2] = target; pc[31:28] = j_adress;
  //   pc_high[3:0] = j_adress; ltz = NF

  // Notes on the sheet:
  //   Input
endmodule

// nor
module ID (
  input  [31:0] in_1,
  output is_add,
  output is_and,
  output is_slt,
  output is_mfhi,
  output is_beq,
  output is_lw,
  output is_kbd,
  output [4:0] rd,
  output [25:0] target,
  output is_sub,
  output is_or,
  output is_sltu,
  output is_mflo,
  output is_bne,
  output is_sw,
  output is_rnd,
  output [4:0] rt,
  output is_mul,
  output is_nor,
  output is_slti,
  output is_blez,
  output is_push,
  output is_tty,
  output [4:0] rs,
  output is_mulu,
  output is_xor,
  output is_sltiu,
  output is_bgtz,
  output is_pop,
  output is_halt,
  output [15:0] offset,
  output is_div,
  output is_bltz,
  output inm,
  output is_divu,
  output is_andi,
  output is_nop,
  output R1,
  output is_ori,
  output is_j,
  output is_addi,
  output R2,
  output is_xori,
  output is_jr,
  output R3
);

  and and_1 (R3, in_1[26], in_1[27], in_1[28], in_1[29], in_1[30], in_1[31]);
  nor nor_1 (R1, in_1[26], in_1[27], in_1[28], in_1[29], in_1[30], in_1[31]);
  or or_1 (inm, is_addi, is_andi, is_ori, is_xori, is_slti, is_sltiu);
  and and_2 (R2, ~in_1[26], ~in_1[27], ~in_1[28], in_1[29], in_1[30], in_1[31]);  // AND_Gate
  and and_3 (is_j, ~in_1[26], ~in_1[27], ~in_1[28], ~in_1[29], in_1[30], ~in_1[31]);  // AND_Gate
  and and_4 (is_addi, ~in_1[26], ~in_1[27], ~in_1[28], in_1[29], ~in_1[30], ~in_1[31]);  // AND_Gate
  and and_5 (is_andi, ~in_1[26], ~in_1[27], in_1[28], in_1[29], ~in_1[30], ~in_1[31]);  // AND_Gate
  and and_6 (is_add, R1, ~in_1[0], ~in_1[1], ~in_1[2], ~in_1[3], ~in_1[4], in_1[5]);  // AND_Gate
  and and_7 (is_sub, R1, ~in_1[0], in_1[1], ~in_1[2], ~in_1[3], ~in_1[4], in_1[5]);  // AND_Gate
  and and_8 (is_mul, R1, ~in_1[0], ~in_1[1], ~in_1[2], in_1[3], in_1[4], ~in_1[5]);  // AND_Gate
  and and_9 (is_mulu, R1, in_1[0], ~in_1[1], ~in_1[2], in_1[3], in_1[4], ~in_1[5]);  // AND_Gate
  and and_10 (is_div, R1, ~in_1[0], in_1[1], ~in_1[2], in_1[3], in_1[4], ~in_1[5]);  // AND_Gate
  and and_11 (is_divu, R1, in_1[0], in_1[1], ~in_1[2], in_1[3], in_1[4], ~in_1[5]);  // AND_Gate
  and and_12 (is_ori, in_1[26], ~in_1[27], in_1[28], in_1[29], ~in_1[30], ~in_1[31]);  // AND_Gate
  and and_13 (is_xori, ~in_1[26], in_1[27], in_1[28], in_1[29], ~in_1[30], ~in_1[31]);  // AND_Gate
  and and_14 (is_slti, ~in_1[26], in_1[27], ~in_1[28], in_1[29], ~in_1[30], ~in_1[31]);  // AND_Gate
  and and_15 (is_sltiu, in_1[26], in_1[27], ~in_1[28], in_1[29], ~in_1[30], ~in_1[31]);  // AND_Gate
  and and_16 (is_and, R1, ~in_1[0], ~in_1[1], in_1[2], ~in_1[3], ~in_1[4], in_1[5]);  // AND_Gate
  and and_17 (is_or, R1, in_1[0], ~in_1[1], in_1[2], ~in_1[3], ~in_1[4], in_1[5]);  // AND_Gate
  and and_18 (is_nor, R1, in_1[0], in_1[1], in_1[2], ~in_1[3], ~in_1[4], in_1[5]);  // AND_Gate
  and and_19 (is_xor, R1, ~in_1[0], ~in_1[1], ~in_1[2], in_1[3], ~in_1[4], in_1[5]);  // AND_Gate
  and and_20 (is_beq, ~in_1[26], ~in_1[27], in_1[28], ~in_1[29], ~in_1[30], ~in_1[31]);  // AND_Gate
  and and_21 (is_bne, in_1[26], ~in_1[27], in_1[28], ~in_1[29], ~in_1[30], ~in_1[31]);  // AND_Gate
  and and_22 (is_blez, ~in_1[26], in_1[27], in_1[28], ~in_1[29], ~in_1[30], ~in_1[31]);  // AND_Gate
  and and_23 (is_bgtz, in_1[26], in_1[27], in_1[28], ~in_1[29], ~in_1[30], ~in_1[31]);  // AND_Gate
  and and_24 (is_bltz, in_1[26], ~in_1[27], ~in_1[28], ~in_1[29], ~in_1[30], ~in_1[31]);  // AND_Gate
  and and_25 (is_lw, in_1[26], in_1[27], ~in_1[28], ~in_1[29], ~in_1[30], in_1[31]);  // AND_Gate
  and and_26 (is_slt, R1, ~in_1[0], in_1[1], ~in_1[2], in_1[3], ~in_1[4], in_1[5]);  // AND_Gate
  and and_27 (is_sltu, R1, in_1[0], in_1[1], ~in_1[2], in_1[3], ~in_1[4], in_1[5]);  // AND_Gate
  and and_28 (is_nop, R1, ~in_1[0], ~in_1[1], ~in_1[2], ~in_1[3], ~in_1[4], ~in_1[5]);  // AND_Gate
  and and_29 (is_sw, in_1[26], in_1[27], ~in_1[28], in_1[29], ~in_1[30], in_1[31]);  // AND_Gate
  and and_30 (is_mfhi, R1, ~in_1[0], ~in_1[1], ~in_1[2], ~in_1[3], in_1[4], ~in_1[5]);  // AND_Gate
  and and_31 (is_mflo, R1, ~in_1[0], in_1[1], ~in_1[2], ~in_1[3], in_1[4], ~in_1[5]);  // AND_Gate
  and and_32 (is_jr, R1, ~in_1[0], ~in_1[1], ~in_1[2], in_1[3], ~in_1[4], ~in_1[5]);  // AND_Gate
  and and_33 (is_pop, R2, ~in_1[0], ~in_1[1], ~in_1[2], ~in_1[3], ~in_1[4], ~in_1[5]);  // AND_Gate
  and and_34 (is_push, R2, in_1[0], ~in_1[1], ~in_1[2], ~in_1[3], ~in_1[4], ~in_1[5]);  // AND_Gate
  and and_35 (is_halt, R3, in_1[0], in_1[1], in_1[2], in_1[3], in_1[4], in_1[5]);
  and and_36 (is_tty, R3, ~in_1[0], in_1[1], ~in_1[2], ~in_1[3], ~in_1[4], ~in_1[5]);  // AND_Gate
  and and_37 (is_kbd, R3, ~in_1[0], ~in_1[1], in_1[2], ~in_1[3], ~in_1[4], ~in_1[5]);  // AND_Gate
  and and_38 (is_rnd, R3, ~in_1[0], in_1[1], ~in_1[2], ~in_1[3], ~in_1[4], ~in_1[5]);  // AND_Gate

  assign offset = in_1[15:0];
  assign rd = in_1[15:11];
  assign rs = in_1[25:21];
  assign rt = in_1[20:16];
  assign target = in_1[25:0];

  // Other names for the same wires on the sheet: add = is_add; addi = is_addi; and = is_and; andi = is_andi;
  //   beq = is_beq; bgtz = is_bgtz; blez = is_blez; bltz = is_bltz; bne = is_bne; div = is_div; divu = is_divu;
  //   halt = is_halt; f0 = in_1[0]; func_code[5:0] = in_1[5:0]; instruction[31:0] = in_1; f1 = in_1[1]; f2 = in_1[2];
  //   f3 = in_1[3]; f4 = in_1[4]; f5 = in_1[5]; o0 = in_1[26]; op_code[5:0] = in_1[31:26]; o1 = in_1[27];
  //   o2 = in_1[28]; o3 = in_1[29]; o4 = in_1[30]; o5 = in_1[31]; J = is_j; jr = is_jr; kbd = is_kbd; lw = is_lw;
  //   mfhi = is_mfhi; mflo = is_mflo; mul = is_mul; mulu = is_mulu; nop = is_nop; nor = is_nor; or = is_or;
  //   ori = is_ori; pop = is_pop; push = is_push; rnd = is_rnd; slt = is_slt; slti = is_slti; sltiu = is_sltiu;
  //   sltu = is_sltu; sub = is_sub; sw = is_sw; tty = is_tty; xor = is_xor; xori = is_xori

  // Notes on the sheet:
  //   INPUT
  //   ARITMETICAS
  //   LOGICAS
  //   COMPARACION
  //   OUTPUT
  //   COPIA A REGISTROS
  //   SALTO
  //   MEMORIA
  //   SPECIAL
  //   REGISTROS
  //   OTROS
endmodule

module Data_Path (
  input  [5:0] func_code,
  input  [6:0] kbd,
  input  [31:0] Instruction,
  input  [5:0] op_code,
  input  rst,
  input  clk,
  input  in_7,
  input  [15:0] offset,
  input  in_9,
  input  kbd_avail,
  input  RW,
  input  enable_md,
  output nop,
  output pop,
  output andi,
  output add,
  output slt,
  output ori,
  output sub,
  output sltu,
  output xori,
  output mult,
  output jr,
  output slti,
  output mulu,
  output mfhi,
  output sltiu,
  output div,
  output mflo,
  output lw,
  output divu,
  output halt,
  output sw,
  output \and ,
  output kbd_2,
  output beq,
  output \or ,
  output rnd,
  output bne,
  output \nor ,
  output tty,
  output blez,
  output \xor ,
  output j,
  output bgtz,
  output push,
  output addi,
  output bltz
);

  wire and_1_out, INM, or_1_out, or_5_out, R1, R2, R3, SF, undriven, ZF;
  wire [2:0] DI_selector;
  wire [4:0] DA, rs_t, rt, srD, srS, srT;
  wire [25:0] target;
  wire [31:0] B, bit_extender_1_out, bit_extender_2_out, branch_control_1_pc_out, DI, Hi, Hi_in, Hi_out, Lo,
       Lo_in, Lo_out, multiplexer_3_out, program_counter_1_out_5, RAM_data, resultALU, RND_t, RS, SP;

  Program_Counter program_counter_1 (
    .in_1(branch_control_1_pc_out), .out_5(program_counter_1_out_5), .clk(clk), .reset(rst));  // open: enable
  Random #(.width(32)) u_RND (.clk(clk), .next(enable_md), .out(RND_t));  // open: clr
  Branch_Control branch_control_1 (
    .bne(blez), .blez(bne), .bgtz(bgtz), .bltz(bltz), .ZF(ZF), .NF(SF), .j(j), .jr(jr), .beq(beq), .rs(RS),
    .pc_in(program_counter_1_out_5), .offset(offset), .target(target), .pc_out(branch_control_1_pc_out));
  or or_1 (or_1_out, add, sub, mult, mulu, div, divu, slt, sltu, \and , \or , \nor , pop, rnd, kbd_2, mfhi, mflo, \xor );
  Register_File register_file_1 (
    .Reset(rst), .RW(in_7), .DI(DI), .Clk(clk), .Stack_Pointer(SP), .DA(DA), .A(rs_t), .B(rt),
    .HI_value(Hi_in), .LO_value(Lo_in), .HI_value_2(Hi_out), .LO_value_2(Lo_out), .RA(RS), .RB(B));  // open: MD
  Multiplexer #(.width(5), .enable("false")) multiplexer_1 (.in0(srT), .in1(srD), .out(DA), .sel(or_1_out));
  assign bit_extender_1_out = {{25{1'b0}}, kbd};  // Bit_Extender bit_extender_1
  or or_2 (DI_selector[0], kbd_2, rnd, mflo);
  or or_3 (DI_selector[1], mfhi, mflo, and_1_out);
  or or_4 (DI_selector[2], and_1_out, kbd_2, lw, pop);
  Multiplexer #(.select(3), .width(32)) multiplexer_2 (
    .in0(resultALU), .in1(RND_t), .in2(Hi), .in3(Lo), .in4(RND_t), .in5(RAM_data), .in6(bit_extender_1_out),
    .in7({32{1'b1}}), .out(DI), .sel(DI_selector));  // open: en
  and and_1 (and_1_out, ~kbd_avail, kbd_2);  // AND_Gate
  assign bit_extender_2_out = {{16{offset[15]}}, offset};  // Bit_Extender bit_extender_2
  Multiplexer #(.width(32)) multiplexer_3 (
    .in0(B), .in1(bit_extender_2_out), .out(multiplexer_3_out), .sel(or_5_out), .en(undriven));
  or or_5 (or_5_out, blez, bgtz, bltz);
  ALU_2 alu_1 (.A(RS), .B(multiplexer_3_out), .RESULT(resultALU), .ZF(ZF), .NF(SF));  // open: in_3, HIGH
  ID id_1 (
    .in_1(Instruction), .is_nop(nop), .is_add(add), .is_sub(sub), .is_mul(mult), .is_mulu(mulu),
    .is_div(div), .is_divu(divu), .is_slt(slt), .is_sltu(sltu), .is_and(\and ), .is_or(\or ), .is_nor(\nor ),
    .is_xor(\xor ), .is_andi(andi), .is_mfhi(mfhi), .is_ori(ori), .is_xori(xori), .is_addi(addi),
    .is_beq(beq), .is_slti(slti), .is_bne(bne), .is_blez(blez), .is_mflo(mflo), .is_sltiu(sltiu),
    .is_bgtz(bgtz), .is_bltz(bltz), .is_lw(lw), .is_sw(sw), .is_j(j), .is_jr(jr), .is_push(push),
    .is_pop(pop), .is_kbd(kbd_2), .is_rnd(rnd), .is_tty(tty), .is_halt(halt), .rd(srD), .rt(srT), .rs(srS),
    .target(target), .offset(offset), .R1(R1), .R3(R3), .R2(R2), .inm(INM));

  assign in_9 = clk;
  assign RW = in_7;

  // Other names for the same wires on the sheet: en_md = enable_md; inst[31:0] = Instruction; KBD_DATA[6:0] = kbd;
  //   kbd_t = kbd_2

  // Notes on the sheet:
  //   Input
  //   Output
endmodule

module _16_32_Sign_Extender (
  input  [15:0] in_1,
  output [31:0] Output
);

  Multiplexer #(.width(16)) multiplexer_1 (
    .in0({16{1'b0}}), .in1({16{1'b1}}), .out(Output[31:16]), .sel(in_1[15]));  // open: en

  assign Output[15:0] = in_1;

  // Notes on the sheet:
  //   SIGN EXTENDER
endmodule

module ALU_Encoder (
  input  is_add,
  input  is_and,
  input  is_slt,
  input  is_sub,
  input  is_or,
  input  is_sltu,
  input  is_mul,
  input  is_nor,
  input  is_slti,
  input  is_mulu,
  input  is_xor,
  input  is_sltiu,
  input  is_div,
  input  is_andi,
  input  is_divu,
  input  is_ori,
  input  is_addi,
  input  is_xori,
  output [3:0] ALU_SEL
);

  wire or_1_out, or_2_out, or_3_out, or_4_out, or_5_out, or_6_out;
  wire [3:0] and_1_out, and_2_out, and_3_out, and_4_out, and_5_out, and_6_out, and_7_out, and_8_out,
       and_9_out, and_10_out, and_11_out, and_12_out, bit_extender_1_out, bit_extender_2_out,
       bit_extender_3_out, bit_extender_4_out, bit_extender_5_out, bit_extender_6_out, bit_extender_7_out,
       bit_extender_8_out, bit_extender_9_out, bit_extender_10_out, bit_extender_11_out, bit_extender_12_out;

  or or_1 (or_1_out, is_add, is_addi);
  or or_2 (or_2_out, is_and, is_andi);
  or or_3 (or_3_out, is_or, is_ori);
  or or_4 (or_4_out, is_xor, is_xori);
  or or_5 (or_5_out, is_slt, is_slti);
  or or_6 (or_6_out, is_sltu, is_sltiu);
  assign bit_extender_1_out = {{3{or_1_out}}, or_1_out};  // Bit_Extender bit_extender_1
  assign bit_extender_2_out = {{3{is_sub}}, is_sub};  // Bit_Extender bit_extender_2
  assign bit_extender_3_out = {{3{is_nor}}, is_nor};  // Bit_Extender bit_extender_3
  assign bit_extender_4_out = {{3{is_mul}}, is_mul};  // Bit_Extender bit_extender_4
  assign bit_extender_5_out = {{3{is_mulu}}, is_mulu};  // Bit_Extender bit_extender_5
  assign bit_extender_6_out = {{3{is_div}}, is_div};  // Bit_Extender bit_extender_6
  assign bit_extender_7_out = {{3{is_divu}}, is_divu};  // Bit_Extender bit_extender_7
  assign bit_extender_8_out = {{3{or_2_out}}, or_2_out};  // Bit_Extender bit_extender_8
  assign bit_extender_9_out = {{3{or_3_out}}, or_3_out};  // Bit_Extender bit_extender_9
  assign bit_extender_10_out = {{3{or_4_out}}, or_4_out};  // Bit_Extender bit_extender_10
  assign bit_extender_11_out = {{3{or_5_out}}, or_5_out};  // Bit_Extender bit_extender_11
  assign bit_extender_12_out = {{3{or_6_out}}, or_6_out};  // Bit_Extender bit_extender_12
  assign and_1_out = bit_extender_1_out & 4'b0001;  // AND_Gate and_1, 4 bits wide
  assign and_2_out = bit_extender_2_out & 4'b0010;  // AND_Gate and_2, 4 bits wide
  assign and_3_out = bit_extender_3_out & 4'b0011;  // AND_Gate and_3, 4 bits wide
  assign and_4_out = bit_extender_4_out & 4'b0100;  // AND_Gate and_4, 4 bits wide
  assign and_5_out = bit_extender_5_out & 4'b0101;  // AND_Gate and_5, 4 bits wide
  assign and_6_out = bit_extender_6_out & 4'b0110;  // AND_Gate and_6, 4 bits wide
  assign and_7_out = bit_extender_7_out & 4'b0111;  // AND_Gate and_7, 4 bits wide
  assign and_8_out = bit_extender_8_out & 4'b1000;  // AND_Gate and_8, 4 bits wide
  assign and_9_out = bit_extender_9_out & 4'b1001;  // AND_Gate and_9, 4 bits wide
  assign and_10_out = bit_extender_10_out & 4'b1010;  // AND_Gate and_10, 4 bits wide
  assign and_11_out = bit_extender_11_out & 4'b1011;  // AND_Gate and_11, 4 bits wide
  assign and_12_out = bit_extender_12_out & 4'b1100;  // AND_Gate and_12, 4 bits wide
  assign ALU_SEL = and_1_out | and_2_out | and_3_out | and_4_out | and_5_out | and_6_out | and_7_out | and_8_out | and_9_out | and_10_out | and_11_out | and_12_out;  // OR_Gate or_7, 4 bits wide

  // Other names for the same wires on the sheet: add = is_add; addi = is_addi; and = is_and; andi = is_andi;
  //   div = is_div; divu = is_divu; mul = is_mul; mulu = is_mulu; nor = is_nor; or = is_or; ori = is_ori;
  //   slt = is_slt; slti = is_slti; sltiu = is_sltiu; sltu = is_sltu; sub = is_sub; xor = is_xor; xori = is_xori

  // Notes on the sheet:
  //   OUTPUT
  //   INPUT 
  //   Operacion 
  //   add
  //   sub
  //   nor
  //   mul
  //   mulu
  //   div
  //   divu
  //   and
  //   or
  //   xor
  //   slt
  //   sltu
  //   Codigo
  //   0001
  //   0010
  //   0011
  //   0100
  //   0101
  //   0110
  //   0111
  //   1000
  //   1001
  //   1010
  //   1011
  //   1100
endmodule

module ALU_2 (
  input  [31:0] A,
  input  [31:0] B,
  input  [3:0] in_3,
  output ZF,
  output [31:0] RESULT,
  output NF,
  output [31:0] HIGH
);

  wire comparator_1_lt, comparator_2_lt, HI_EN, not_1_out;
  wire [31:0] AND, DIV, DIV_HIGH, DIVU, DIVU_HIGH, MUL, MUL_HIGH, MULU, MULU_HIGH, NOR, OR, SLT, SLTU, SUB,
       SUM, XOR;

  Adder #(.width(32)) adder_1 (.a(A), .b(B), .out(SUM));  // open: cin, cout
  Subtractor #(.width(32)) subtractor_1 (.a(A), .b(B), .out(SUB));  // open: bin, bout
  Comparator #(.width(32)) comparator_1 (.a(A), .b(B), .lt(comparator_1_lt));  // open: gt, eq
  Comparator #(.width(32), .mode("unsigned")) comparator_2 (.a(A), .b(B), .lt(comparator_2_lt));  // open: gt, eq
  assign SLT = {{31{1'b0}}, comparator_1_lt};  // Bit_Extender bit_extender_1
  assign SLTU = {{31{1'b0}}, comparator_2_lt};  // Bit_Extender bit_extender_2
  assign AND = A & B;  // AND_Gate and_1, 32 bits wide
  assign NOR = ~(A | B);  // NOR_Gate nor_1, 32 bits wide
  assign XOR = A ^ B;  // XOR_Gate xor_1, 32 bits wide
  assign OR = A | B;  // OR_Gate or_1, 32 bits wide
  MULU mulu_1 (.A(A), .B(B), .L(MULU), .H(MULU_HIGH));
  DIVU divu_1 (.A(A), .B(B), .L(DIVU), .H(DIVU_HIGH));
  Multiplier #(.width(32)) multiplier_1 (.a(A), .b(B), .out(MUL), .cout(MUL_HIGH));  // open: cin
  Divider #(.width(32)) divider_1 (.a(A), .b(B), .out(DIV), .rem(DIV_HIGH));  // open: upper
  Multiplexer #(.select(2), .width(32)) multiplexer_1 (
    .in0(MUL_HIGH), .in1(MULU_HIGH), .in2(DIV_HIGH), .in3(DIVU_HIGH), .out(HIGH), .sel(in_3[1:0]), .en(HI_EN));
  not not_1 (not_1_out, in_3[3]);
  and and_2 (HI_EN, in_3[2], not_1_out);
  Multiplexer #(.select(4), .width(32), .disabled(0), .enable("false")) multiplexer_2 (
    .in0(A), .in1(SUM), .in2(SUB), .in3(NOR), .in4(NOR), .in5(MUL), .in6(MULU), .in7(DIV), .in8(DIVU),
    .in9(AND), .in10(OR), .in11(XOR), .in12(SLT), .in13(SLTU), .out(RESULT), .sel(in_3));  // open: in14, in15
  Comparator #(.width(32)) comparator_3 (.a(RESULT), .b({32{1'b0}}), .eq(ZF), .lt(NF));  // open: gt

  // Other names for the same wires on the sheet: HI_S[1:0] = in_3[1:0]; Selector[3:0] = in_3; B2 = in_3[2];
  //   B3 = in_3[3]

  // Notes on the sheet:
  //   INPUT
  //   OPS
  //   OUTPUT
endmodule

module MULU (
  input  [31:0] A,
  input  [31:0] B,
  output [31:0] L,
  output [31:0] H
);

  wire [31:0] abs_1_a_2, abs_2_a_2;

  ABS abs_1 (.A(A), .A_2(abs_1_a_2));
  ABS abs_2 (.A(B), .A_2(abs_2_a_2));
  Multiplier #(.width(32)) multiplier_1 (.a(abs_1_a_2), .b(abs_2_a_2), .out(L), .cout(H));  // open: cin

  // Other names for the same wires on the sheet: MULU_HIGH[31:0] = H; MULU_LOW[31:0] = L

  // Notes on the sheet:
  //   INPUT
  //   OUTPUT
endmodule

module DIVU (
  input  [31:0] A,
  input  [31:0] B,
  output [31:0] L,
  output [31:0] H
);

  wire [31:0] abs_1_a_2, abs_2_a_2;

  ABS abs_1 (.A(A), .A_2(abs_1_a_2));
  ABS abs_2 (.A(B), .A_2(abs_2_a_2));
  Multiplier #(.width(32)) multiplier_1 (.a(abs_1_a_2), .b(abs_2_a_2), .out(L), .cout(H));  // open: cin

  // Other names for the same wires on the sheet: DIVU_HIGH[31:0] = H; DIVU_LOW[31:0] = L

  // Notes on the sheet:
  //   INPUT
  //   OUTPUT
endmodule

module Program_Counter (
  input  [31:0] in_1,
  input  clk,
  input  reset,
  input  enable,
  output [31:0] out_5
);

  Register #(.width(32), .trigger("falling")) PROGRAM_COUNTER (
    .D(in_1), .en(enable), .Q(out_5), .clk(clk), .clr(reset));

  // Other names for the same wires on the sheet: e = enable; pc_in[31:0] = in_1; pc_out[31:0] = out_5; rst = reset

  // Notes on the sheet:
  //   INPUT
  //   OUTPUT
endmodule
